// Logisim project 2105105.circ as structural Verilog: 2 circuits, main circuit main
module main (
  input  CS2,
  input  CS1,
  input  CS0,
  input  B3,
  input  B2,
  input  B1,
  input  B0,
  input  A3,
  input  A2,
  input  A1,
  input  A0,
  output Cout,
  output S,
  output V,
  output out_15,
  output out_16,
  output out_17,
  output out_18,
  output Z
);

  wire n7404_1_p2, n7404_1_p4, n7404_1_p6, n7404_1_p7, n7404_2_p2, n7404_2_p4, n7404_2_p6, n7404_2_p8,
       n7408_1_p3, n7408_1_p6, n7408_1_p9, n7408_1_p12, n7408_2_p3, n7408_2_p6, n7408_2_p9, n7408_2_p12,
       n7408_3_p3, n7408_3_p5, n7408_3_p6, n7432_2_p6, n7432_2_p9, n7483_1_p8, n7486_1_p3, n7486_1_p6,
       n7486_1_p9, n7486_1_p12, n74157_1_p2, n74157_1_p3, n74157_1_p4, n74157_1_p5, n74157_1_p6, n74157_1_p7,
       n74157_1_p11, n74157_1_p12, n74157_1_p13, n74157_1_p14, n74157_1_p15, n74157_1_p16, n74157_3_p3,
       n74157_3_p4, n74157_3_p6, n74157_3_p7, n74157_3_p12, n74157_3_p13, n74157_3_p15, n74157_3_p16;

  // _7404 7404_1: pin names not known; wires that end beside it: CS2, n7404_1_p2, CS1, n7404_1_p4, CS0, n7404_1_p6, n7404_1_p7, Z
  // _7408 7408_1: pin names not known; wires that end beside it: n7404_1_p4, B3, n7408_1_p3, n7404_1_p4, B2, n7408_1_p6, n7404_1_p4, B1, n7408_1_p9, n7404_1_p4, B0, n7408_1_p12
  // _7408 7408_2: pin names not known; wires that end beside it: CS1, n7404_1_p2, n7408_2_p3, n7408_2_p3, CS0, n7408_2_p6, CS1, CS2, n7408_2_p9, n7408_2_p9, n7404_1_p6, n7408_2_p12
  // _7486 7486_1: pin names not known; wires that end beside it: B3, A3, n7486_1_p3, B2, A2, n7486_1_p6, A1, B1, n7486_1_p9, A0, B0, n7486_1_p12
  // _7404 7404_2: pin names not known; wires that end beside it: B3, n7404_2_p2, B2, n7404_2_p4, B1, n7404_2_p6, B0, n7404_2_p8
  // _74157 74157_1: pin names not known; wires that end beside it: n7408_2_p12, n74157_1_p2, n74157_1_p3, n74157_1_p4, n74157_1_p5, n74157_1_p6, n74157_1_p7, 1'b0, 1'b1, 1'b0, n74157_1_p11, n74157_1_p12, n74157_1_p13, n74157_1_p14, n74157_1_p15, n74157_1_p16
  // _74157 74157_2: pin names not known; wires that end beside it: n7408_2_p6, A3, n7486_1_p3, n74157_1_p2, A2, n7486_1_p6, n74157_1_p5, 1'b0, 1'b1, 1'b0, A1, n7486_1_p9, n74157_1_p14, A0, n7486_1_p12, n74157_1_p11
  // _7408 7408_3: pin names not known; wires that end beside it: n7408_2_p3, n7404_1_p6, n7408_3_p3, CS0, n7408_3_p5, n7408_3_p6
  // _7486 7486_2: pin names not known; wires that end beside it: 1'b1, n74157_1_p2, n74157_1_p3, 1'b1, n74157_1_p5, n74157_1_p6, 1'b1, n74157_1_p14, n74157_1_p15, n74157_1_p11, 1'b1, n74157_1_p12
  // _74157 74157_3: pin names not known; wires that end beside it: n7408_3_p3, n7408_1_p3, n74157_3_p3, n74157_3_p4, n7408_1_p6, n74157_3_p6, n74157_3_p7, 1'b0, 1'b1, 1'b0, n7408_1_p9, n74157_3_p12, n74157_3_p13, n7408_1_p12, n74157_3_p15, n74157_3_p16
  // _7432 7432_1: pin names not known; wires that end beside it: n7404_2_p2, n7408_1_p3, n74157_3_p3, n7404_2_p4, n7408_1_p6, n74157_3_p6, n7404_2_p6, n7408_1_p9, n74157_3_p12, n7404_2_p8, n7408_1_p12, n74157_3_p15
  // _7432 7432_2: pin names not known; wires that end beside it: n7404_1_p4, CS2, n7408_3_p5, out_15, out_16, n7432_2_p6, n7432_2_p6, out_17, n7432_2_p9, n7432_2_p9, V, n7404_1_p7
  // _7483 7483_1: pin names not known; wires that end beside it: 1'b0, 1'b0, 1'b0, Cout, 1'b0, 1'b0, 1'b0, n7483_1_p8, n74157_3_p4, n74157_1_p4, out_15
  // _7483 7483_2: pin names not known; wires that end beside it: 1'b0, out_16, n74157_1_p7, n74157_3_p7, out_17, n74157_3_p13, n74157_1_p16, 1'b0, n7483_1_p8, n7408_3_p6, 1'b0, n74157_3_p16, n74157_1_p13, out_18
  // _7486 7486_3: pin names not known; wires that end beside it: Cout, n7483_1_p8, V, 1'b0, 1'b1

  assign S = out_15;

  // Notes on the sheet:
  //   cs2'cs1cs0
  //   cs2cs1cs0'
  //   3
  //   2
  //   2
  //   3
  //   1
  //   0
  //   0
  //   1
  //   3
  //   2
  //   1
  //   0
  //   cs2'cs1cs0'
  //   3
  //   cs1'B
  //   2
  //   1
  //   0
  //   3
  //   2
  //   1
  //   B'
  //   0
  //   Func :
  //   3
  //   cs1'B  +
  //   B'
  //   2
  //   1
  //   0
  //   Zin
  //   c4
  //   Xi
  //   3
  //   Cin = Cout1
  //   Yi
  //   c3
endmodule

module For_A (
  input  CS2,
  input  CS1,
  input  CS0,
  input  B3,
  input  B2,
  input  B1,
  input  B0,
  input  A3,
  input  A2,
  input  A1,
  input  A0,
  output out_12,
  output out_13,
  output out_14,
  output out_15,
  output out_16,
  output out_17,
  output out_18,
  output out_19,
  output Cout,
  output S,
  output V,
  output out_23,
  output out_24,
  output out_25,
  output out_26,
  output Z
);

  wire n7404_1_p2, n7404_1_p4, n7404_1_p6, n7404_1_p7, n7404_2_p2, n7404_2_p4, n7404_2_p6, n7404_2_p8,
       n7408_1_p3, n7408_1_p6, n7408_1_p9, n7408_1_p12, n7408_2_p3, n7408_2_p6, n7408_2_p9, n7408_2_p12,
       n7408_3_p3, n7408_3_p5, n7408_3_p6, n7432_2_p6, n7432_2_p9, n7483_1_p8, n7486_1_p3, n7486_1_p6,
       n7486_1_p9, n7486_1_p12, n74157_1_p2, n74157_1_p3, n74157_1_p5, n74157_1_p6, n74157_1_p11,
       n74157_1_p12, n74157_1_p14, n74157_1_p15, n74157_3_p3, n74157_3_p6, n74157_3_p12, n74157_3_p15;

  // _7404 7404_1: pin names not known; wires that end beside it: CS2, n7404_1_p2, CS1, n7404_1_p4, CS0, n7404_1_p6, n7404_1_p7, Z
  // _7408 7408_1: pin names not known; wires that end beside it: n7404_1_p4, B3, n7408_1_p3, n7404_1_p4, B2, n7408_1_p6, n7404_1_p4, B1, n7408_1_p9, n7404_1_p4, B0, n7408_1_p12
  // _7408 7408_2: pin names not known; wires that end beside it: CS1, n7404_1_p2, n7408_2_p3, n7408_2_p3, CS0, n7408_2_p6, CS1, CS2, n7408_2_p9, n7408_2_p9, n7404_1_p6, n7408_2_p12
  // _7486 7486_1: pin names not known; wires that end beside it: B3, A3, n7486_1_p3, B2, A2, n7486_1_p6, A1, B1, n7486_1_p9, A0, B0, n7486_1_p12
  // _7404 7404_2: pin names not known; wires that end beside it: B3, n7404_2_p2, B2, n7404_2_p4, B1, n7404_2_p6, B0, n7404_2_p8
  // _74157 74157_1: pin names not known; wires that end beside it: n7408_2_p12, n74157_1_p2, n74157_1_p3, out_12, n74157_1_p5, n74157_1_p6, out_13, 1'b0, 1'b1, 1'b0, n74157_1_p11, n74157_1_p12, out_15, n74157_1_p14, n74157_1_p15, out_14
  // _74157 74157_2: pin names not known; wires that end beside it: n7408_2_p6, A3, n7486_1_p3, n74157_1_p2, A2, n7486_1_p6, n74157_1_p5, 1'b0, 1'b1, 1'b0, A1, n7486_1_p9, n74157_1_p14, A0, n7486_1_p12, n74157_1_p11
  // _7408 7408_3: pin names not known; wires that end beside it: n7408_2_p3, n7404_1_p6, n7408_3_p3, CS0, n7408_3_p5, n7408_3_p6
  // _7486 7486_2: pin names not known; wires that end beside it: 1'b1, n74157_1_p2, n74157_1_p3, 1'b1, n74157_1_p5, n74157_1_p6, 1'b1, n74157_1_p14, n74157_1_p15, n74157_1_p11, 1'b1, n74157_1_p12
  // _74157 74157_3: pin names not known; wires that end beside it: n7408_3_p3, n7408_1_p3, n74157_3_p3, out_16, n7408_1_p6, n74157_3_p6, out_17, 1'b0, 1'b1, 1'b0, n7408_1_p9, n74157_3_p12, out_18, n7408_1_p12, n74157_3_p15, out_19
  // _7432 7432_1: pin names not known; wires that end beside it: n7404_2_p2, n7408_1_p3, n74157_3_p3, n7404_2_p4, n7408_1_p6, n74157_3_p6, n7404_2_p6, n7408_1_p9, n74157_3_p12, n7404_2_p8, n7408_1_p12, n74157_3_p15
  // _7432 7432_2: pin names not known; wires that end beside it: n7404_1_p4, CS2, n7408_3_p5, out_23, out_24, n7432_2_p6, n7432_2_p6, out_25, n7432_2_p9, n7432_2_p9, V, n7404_1_p7
  // _7483 7483_1: pin names not known; wires that end beside it: 1'b0, 1'b0, 1'b0, Cout, 1'b0, 1'b0, 1'b0, n7483_1_p8, out_16, out_12, out_23
  // _7483 7483_2: pin names not known; wires that end beside it: 1'b0, out_24, out_13, out_17, out_25, out_18, out_14, 1'b0, n7483_1_p8, n7408_3_p6, 1'b0, out_19, out_15, out_26
  // _7486 7486_3: pin names not known; wires that end beside it: Cout, n7483_1_p8, V, 1'b0, 1'b1

  assign S = out_23;

  // Notes on the sheet:
  //   cs2'cs1cs0
  //   cs2cs1cs0'
  //   3
  //   2
  //   2
  //   3
  //   1
  //   0
  //   1
  //   0
  //   3
  //   Xi
  //   2
  //   1
  //   0
  //   cs2'cs1cs0'
  //   3
  //   cs1'B
  //   2
  //   1
  //   0
  //   3
  //   2
  //   1
  //   B'
  //   0
  //   3
  //   cs1'B  +
  //   B'
  //   2
  //   1
  //   0
  //   Zin
  //   c4
  //   3
  //   Yi
  //   Cin = Cout1
  //   Func :
  //   c3
endmodule
